// Logisim project SPEAR2_logisim1.circ as structural Verilog: 1 circuit, main circuit main
module main (
  input  in_1
);

  wire adder_2_cout, and_3_out, BR_A, BR_B, BR_PC, BR_PC_C, BR_PC_N, BR_PC_Z, BR_RAM, BR_RP, BR_RPL, BR_SP,
       BR_STAT, BW_A, BW_ADD, BW_B, BW_COM, BW_LIT, BW_NOR, BW_PC, BW_RAM, BW_RP, BW_RPL, BW_SP, BW_STAT,
       CLK, CLK2, nor_1_out, RST_IR_CNT;
  wire [1:0] counter_1_q;
  wire [3:0] and_1_out;
  wire [7:0] adder_1_out, adder_2_out, AH, AL, BH, BL, BUSH, BUSL, controlled_buffer_1_out,
       controlled_buffer_2_out, controlled_buffer_11_out, controlled_buffer_12_out, IR1, IR2, IR3, PCH, PCL,
       ram_1_data, rom_1_data, RPH_q, RPL_q;

  Clock clock_1 (.out(CLK));
  not not_1 (CLK2, CLK);
  Counter #(.width(2), .max('h3)) counter_1 (
    .Q(counter_1_q), .clk(CLK2), .clr(RST_IR_CNT));  // open: load, D, count, carry
  assign and_1_out = IR1[3:0] & {4{in_1}};  // AND_Gate and_1, 4 bits wide
  Register u_IR1 (.D(rom_1_data), .en(nor_1_out), .Q(IR1), .clk(CLK));  // open: clr
  nor nor_1 (nor_1_out, counter_1_q[0], counter_1_q[1]);
  Decoder #(.select(4)) decoder_1 (
    .out0(BW_LIT), .out1(BW_A), .out2(BW_B), .out3(BW_PC), .out4(BW_SP), .out5(BW_STAT), .out6(BW_RP),
    .out7(BW_RPL), .out8(BW_RAM), .out10(BW_ADD), .out11(BW_COM), .out12(BW_NOR), .sel(IR1[7:4]));  // open: out9, out13, out14, out15, en
  Decoder #(.select(4)) decoder_2 (
    .out1(BR_A), .out2(BR_B), .out3(BR_PC), .out4(BR_SP), .out5(BR_STAT), .out6(BR_RP), .out7(BR_RPL),
    .out8(BR_RAM), .out10(BR_PC_N), .out11(BR_PC_Z), .out12(BR_PC_C), .sel(and_1_out));  // open: out0, out9, out13, out14, out15, en
  ROM #(.addrWidth(16)) rom_1 (.addr({PCH, PCL}), .data(rom_1_data));  // open: sel
  Register u_IR2 (.D(rom_1_data), .en(counter_1_q[0]), .Q(IR2), .clk(CLK));  // open: clr
  Register u_IR3 (.D(rom_1_data), .en(counter_1_q[1]), .Q(IR3), .clk(CLK));  // open: clr
  // AND_Gate and_2 has open pins: in0=counter_1_q[0], in1=counter_1_q[1], out=open
  and and_3 (and_3_out, counter_1_q[0], BW_LIT);
  buf or_1 (RST_IR_CNT, and_3_out);  // OR_Gate
  // NOT_Gate not_2 is placed but not wired
  Hex_Digit_Display hex_digit_display_1 (.value(BUSH[7:4]));  // open: dp
  Pull_Resistor pull_resistor_1 (.node(BUSH));
  Hex_Digit_Display hex_digit_display_2 (.value(BUSH[3:0]));  // open: dp
  Hex_Digit_Display hex_digit_display_3 (.value(BUSL[7:4]));  // open: dp
  Pull_Resistor pull_resistor_2 (.node(BUSL));
  Adder adder_1 (.a(PCH), .b({8{1'b0}}), .out(adder_1_out), .cin(adder_2_cout));  // open: cout
  Controlled_Buffer #(.width(8)) controlled_buffer_1 (.in(adder_1_out), .out(controlled_buffer_1_out));  // open: en
  Adder adder_2 (.a(PCL), .b(8'h1), .out(adder_2_out), .cout(adder_2_cout));  // open: cin
  Controlled_Buffer #(.width(8)) controlled_buffer_2 (.in(adder_2_out), .out(controlled_buffer_2_out));  // open: en
  Hex_Digit_Display hex_digit_display_4 (.value(BUSL[3:0]));  // open: dp
  assign controlled_buffer_1_out = BR_RP ? BUSH : 8'bz;  // Controlled_Buffer controlled_buffer_3
  assign controlled_buffer_2_out = BR_RP ? BUSL : 8'bz;  // Controlled_Buffer controlled_buffer_4
  Register u_AH (.D(BUSH), .Q(AH));  // open: en, clk, clr
  Register u_AL (.D(BUSL), .Q(AL));  // open: en, clk, clr
  Register u_BH (.D(BUSH), .Q(BH));  // open: en, clk, clr
  Register u_BL (.D(BUSL), .Q(BL));  // open: en, clk, clr
  Register u_PCH (.D(controlled_buffer_1_out), .Q(PCH));  // open: en, clk, clr
  Register u_PCL (.D(controlled_buffer_2_out), .Q(PCL));  // open: en, clk, clr
  Controlled_Buffer #(.width(8)) controlled_buffer_5 (.in(AH), .out(BUSH));  // open: en
  Controlled_Buffer #(.width(8)) controlled_buffer_6 (.in(AL), .out(BUSL));  // open: en
  Controlled_Buffer #(.width(8)) controlled_buffer_7 (.in(BH), .out(BUSH));  // open: en
  Controlled_Buffer #(.width(8)) controlled_buffer_8 (.in(BL), .out(BUSL));  // open: en
  Controlled_Buffer #(.width(8)) controlled_buffer_9 (.in(PCH), .out(BUSH));  // open: en
  Controlled_Buffer #(.width(8)) controlled_buffer_10 (.in(PCL), .out(BUSL));  // open: en
  Register RPH (.Q(RPH_q));  // open: D, en, clk, clr
  Register RPL (.Q(RPL_q));  // open: D, en, clk, clr
  Controlled_Buffer #(.width(8)) controlled_buffer_11 (.in(RPH_q), .out(controlled_buffer_11_out));  // open: en
  Controlled_Buffer #(.width(8)) controlled_buffer_12 (.in(RPL_q), .out(controlled_buffer_12_out));  // open: en
  RAM #(.addrWidth(16)) ram_1 (
    .addr({controlled_buffer_11_out, controlled_buffer_12_out}), .data(ram_1_data));  // open: sel, clk, ld, clr
  Controlled_Buffer #(.width(8)) controlled_buffer_13 (.in(ram_1_data), .out(BUSL));  // open: en
  Controlled_Buffer #(.width(8)) controlled_buffer_14 (.in(ram_1_data), .out(BUSL));  // open: en

  // Other names for the same wires on the sheet: EN_BR = in_1

  // Notes on the sheet:
  //   contents of rom_1 (hex, n*v repeats v):
  //   1 44 33 2 0 f0 6 0 50 a8 7 51 a8
endmodule
