// Logisim project hera_logisim1.circ as structural Verilog: 1 circuit, main circuit main
module main (
);

  wire ADD_C, adder_2_cout, adder_4_cout, adder_6_cout, and_1_out, and_2_out, and_3_out, and_5_out,
       and_6_out, and_7_out, and_8_out, and_9_out, and_10_out, and_14_out, and_15_out, and_16_out,
       and_17_out, BR_A, BR_A_B, BR_A_D, BR_B, BR_B_D, BR_B_RP, BR_C, BR_C_D, BR_C_PC, BR_PC, BR_PC_C,
       BR_PC_D, BR_PC_N, BR_PC_Z, BR_RAM, BR_RP, BR_RP_D, BR_STAT, BW_A, BW_ADD, BW_B, BW_C, BW_COM, BW_LIT,
       BW_NOR, BW_PC, BW_RAM, BW_RP, BW_STAT, CLK, CLK2, COM_C, comparator_1_eq, comparator_2_eq,
       comparator_3_eq, comparator_4_eq, comparator_5_eq, comparator_6_eq, d_ff_1_q, decoder_1_out0,
       decoder_1_out1, decoder_1_out2, decoder_1_out3, EN_BR, not_2_out, not_3_out, not_4_out, not_5_out,
       not_8_out, or_3_out, or_8_out, or_9_out, RST_IR_CNT;
  wire [1:0] counter_1_q;
  wire [7:0] adder_1_out, adder_2_out, adder_3_out, adder_4_out, adder_5_out, adder_6_out, AH, AL,
       and_12_out, and_13_out, BH, BL, BUSH, BUSL, button_1_out, CH, CL, controlled_buffer_1_out,
       controlled_buffer_2_out, GPOAH_q, GPOAL_q, IR1, IR2, IR3, joystick_1_y, nor_1_out, nor_2_out,
       not_6_out, not_7_out, or_10_out, PCH, PCL, rom_1_data, RPH, RPL, STAT, STAT_D, STAT_OW;

  Clock clock_1 (.out(CLK));
  not not_1 (CLK2, CLK);
  Counter #(.width(2), .max('h3)) counter_1 (
    .Q(counter_1_q), .clk(CLK2), .clr(RST_IR_CNT));  // open: load, D, count, carry
  Decoder #(.select(2)) decoder_1 (
    .out0(decoder_1_out0), .out1(decoder_1_out1), .out2(decoder_1_out2), .out3(decoder_1_out3),
    .sel(counter_1_q));  // open: en
  Register u_IR1 (.D(rom_1_data), .en(decoder_1_out0), .Q(IR1), .clk(CLK));  // open: clr
  Demultiplexer #(.select(4)) demultiplexer_1 (
    .out1(BR_A_D), .out2(BR_B_D), .out3(BR_C_D), .out4(BR_RAM), .out5(BR_RP_D), .out6(BR_PC_D),
    .out7(BR_STAT), .out10(BR_A_B), .out11(BR_B_RP), .out12(BR_C_PC), .out13(BR_PC_C), .out14(BR_PC_Z),
    .out15(BR_PC_N), .in(EN_BR), .sel(IR1[3:0]));  // open: out0, out8, out9, en
  ROM #(.addrWidth(16)) rom_1 (.addr({PCH, PCL}), .data(rom_1_data));  // open: sel
  Register u_IR2 (.D(rom_1_data), .en(decoder_1_out1), .Q(IR2), .clk(CLK));  // open: clr
  Decoder #(.select(4)) decoder_2 (
    .out0(BW_LIT), .out1(BW_A), .out2(BW_B), .out3(BW_C), .out4(BW_RAM), .out5(BW_RP), .out6(BW_PC),
    .out7(BW_STAT), .out10(BW_ADD), .out11(BW_COM), .out12(BW_NOR), .sel(IR1[7:4]));  // open: out8, out9, out13, out14, out15, en
  Register u_IR3 (.D(rom_1_data), .en(decoder_1_out2), .Q(IR3), .clk(CLK));  // open: clr
  and and_1 (and_1_out, BR_PC_N, STAT[2]);
  or or_1 (BR_PC, BR_PC_D, BR_C_PC, and_1_out, and_2_out, and_3_out);
  and and_2 (and_2_out, BR_PC_Z, STAT[1]);
  and and_3 (and_3_out, BR_PC_C, STAT[0]);
  or or_2 (BR_A, BR_A_D, BR_A_B);
  or or_3 (or_3_out, BR_B_D, BR_A_B);
  or or_4 (BR_B, or_3_out, BR_B_RP);
  or or_5 (BR_RP, BR_RP_D, BR_B_RP);
  or or_6 (BR_C, BR_C_D, BR_C_PC);
  and and_4 (RST_IR_CNT, decoder_1_out2, not_2_out);
  not not_2 (not_2_out, BW_LIT);
  and and_5 (and_5_out, decoder_1_out1, not_2_out);
  and and_6 (and_6_out, decoder_1_out3, BW_LIT);
  or or_7 (EN_BR, and_5_out, and_6_out);
  Hex_Digit_Display hex_digit_display_1 (.value(BUSH[3:0]));  // open: dp
  Hex_Digit_Display hex_digit_display_2 (.value(BUSH[7:4]));  // open: dp
  Pull_Resistor pull_resistor_1 (.node(BUSH));
  Adder adder_1 (.a(PCH), .b({8{1'b0}}), .out(adder_1_out), .cin(adder_2_cout));  // open: cout
  Adder adder_2 (.a(PCL), .b(8'h1), .out(adder_2_out), .cout(adder_2_cout));  // open: cin
  Hex_Digit_Display hex_digit_display_3 (.value(BUSL[7:4]));  // open: dp
  Hex_Digit_Display hex_digit_display_4 (.value(BUSL[3:0]));  // open: dp
  Pull_Resistor pull_resistor_2 (.node(BUSL));
  assign controlled_buffer_1_out = not_3_out ? adder_1_out : 8'bz;  // Controlled_Buffer controlled_buffer_1
  assign controlled_buffer_2_out = not_3_out ? adder_2_out : 8'bz;  // Controlled_Buffer controlled_buffer_2
  not not_3 (not_3_out, BR_PC);
  not not_4 (not_4_out, d_ff_1_q);
  D_Flip_Flop d_ff_1 (.clk(CLK), .D(EN_BR), .Q(d_ff_1_q));  // open: Qn, preset, en, reset
  assign STAT_D = not_5_out ? STAT_OW : 8'bz;  // Controlled_Buffer controlled_buffer_3
  not not_5 (not_5_out, BR_STAT);
  or or_8 (or_8_out, BR_STAT, BW_ADD, BW_COM, BW_NOR);
  assign controlled_buffer_1_out = BR_PC ? BUSH : 8'bz;  // Controlled_Buffer controlled_buffer_4
  assign controlled_buffer_2_out = BR_PC ? BUSL : 8'bz;  // Controlled_Buffer controlled_buffer_5
  or or_9 (or_9_out, BR_PC, not_4_out);
  assign STAT_D = BR_STAT ? BUSL : 8'bz;  // Controlled_Buffer controlled_buffer_6
  and and_7 (and_7_out, or_8_out, EN_BR);
  Register u_AH (.D(BUSH), .en(BR_A), .Q(AH), .clk(CLK));  // open: clr
  Register u_AL (.D(BUSL), .en(BR_A), .Q(AL), .clk(CLK));  // open: clr
  Register u_BH (.D(BUSH), .en(BR_B), .Q(BH), .clk(CLK));  // open: clr
  Register u_BL (.D(BUSL), .en(BR_B), .Q(BL), .clk(CLK));  // open: clr
  Register u_CH (.D(BUSH), .en(BR_C), .Q(CH), .clk(CLK));  // open: clr
  Register u_CL (.D(BUSL), .en(BR_C), .Q(CL), .clk(CLK));  // open: clr
  Register u_PCH (.D(controlled_buffer_1_out), .en(or_9_out), .Q(PCH), .clk(CLK2));  // open: clr
  Register u_PCL (.D(controlled_buffer_2_out), .en(or_9_out), .Q(PCL), .clk(CLK2));  // open: clr
  Register u_STAT (.D(STAT_D), .en(and_7_out), .Q(STAT), .clk(CLK));  // open: clr
  assign BUSH = BW_A ? AH : 8'bz;  // Controlled_Buffer controlled_buffer_7
  assign BUSL = BW_A ? AL : 8'bz;  // Controlled_Buffer controlled_buffer_8
  assign BUSH = BW_B ? BH : 8'bz;  // Controlled_Buffer controlled_buffer_9
  assign BUSL = BW_B ? BL : 8'bz;  // Controlled_Buffer controlled_buffer_10
  assign BUSH = BW_C ? CH : 8'bz;  // Controlled_Buffer controlled_buffer_11
  assign BUSL = BW_C ? CL : 8'bz;  // Controlled_Buffer controlled_buffer_12
  assign BUSH = BW_PC ? PCH : 8'bz;  // Controlled_Buffer controlled_buffer_13
  assign BUSL = BW_PC ? PCL : 8'bz;  // Controlled_Buffer controlled_buffer_14
  assign BUSH = BW_LIT ? IR2 : 8'bz;  // Controlled_Buffer controlled_buffer_15
  assign BUSL = BW_LIT ? IR3 : 8'bz;  // Controlled_Buffer controlled_buffer_16
  assign BUSL = BW_STAT ? STAT : 8'bz;  // Controlled_Buffer controlled_buffer_17
  assign not_6_out = ~AH;  // NOT_Gate not_6, 8 bits wide
  assign not_7_out = ~AL;  // NOT_Gate not_7, 8 bits wide
  Register u_RPH (.D(BUSH), .en(BR_RP), .Q(RPH), .clk(CLK));  // open: clr
  Register u_RPL (.D(BUSL), .en(BR_RP), .Q(RPL), .clk(CLK));  // open: clr
  assign BUSH = BW_ADD ? adder_3_out : 8'bz;  // Controlled_Buffer controlled_buffer_18
  Adder adder_3 (.a(AH), .b(BH), .out(adder_3_out), .cin(adder_4_cout), .cout(ADD_C));
  assign BUSL = BW_ADD ? adder_4_out : 8'bz;  // Controlled_Buffer controlled_buffer_19
  Adder adder_4 (.a(AL), .b(BL), .out(adder_4_out), .cout(adder_4_cout));  // open: cin
  assign BUSH = BW_NOR ? nor_1_out : 8'bz;  // Controlled_Buffer controlled_buffer_20
  assign nor_1_out = ~(AH | BH);  // NOR_Gate nor_1, 8 bits wide
  assign nor_2_out = ~(AL | BL);  // NOR_Gate nor_2, 8 bits wide
  assign BUSL = BW_NOR ? nor_2_out : 8'bz;  // Controlled_Buffer controlled_buffer_21
  Comparator #(.mode("unsigned")) comparator_1 (.a(BUSH), .b({8{1'b0}}), .eq(comparator_1_eq));  // open: gt, lt
  Comparator #(.mode("unsigned")) comparator_2 (.a(BUSL), .b({8{1'b0}}), .eq(comparator_2_eq));  // open: gt, lt
  and and_8 (and_8_out, BW_ADD, ADD_C);
  and and_9 (and_9_out, BW_COM, COM_C);
  and and_10 (and_10_out, BW_NOR, BUSL[0]);
  assign BUSH = BW_RP ? RPH : 8'bz;  // Controlled_Buffer controlled_buffer_22
  assign BUSL = BW_RP ? RPL : 8'bz;  // Controlled_Buffer controlled_buffer_23
  Adder adder_5 (.a(not_6_out), .b({8{1'b0}}), .out(adder_5_out), .cin(adder_6_cout), .cout(COM_C));
  assign BUSH = BW_COM ? adder_5_out : 8'bz;  // Controlled_Buffer controlled_buffer_24
  assign BUSL = BW_COM ? adder_6_out : 8'bz;  // Controlled_Buffer controlled_buffer_25
  Adder adder_6 (.a(not_7_out), .b(8'h1), .out(adder_6_out), .cout(adder_6_cout));  // open: cin
  and and_11 (or_10_out[1], comparator_1_eq, comparator_2_eq);
  or or_10 (or_10_out[0], and_8_out, and_9_out, and_10_out);
  assign and_12_out = STAT & 8'hf8;  // AND_Gate and_12, 8 bits wide
  assign and_13_out = {or_10_out[7:3], BUSH[7], or_10_out[1:0]} & 8'h7;  // AND_Gate and_13, 8 bits wide
  assign STAT_OW = and_12_out | and_13_out;  // OR_Gate or_11, 8 bits wide
  and and_14 (and_14_out, BR_RAM, CLK);
  and and_15 (and_15_out, BW_RAM, not_8_out);
  not not_8 (not_8_out, comparator_3_eq);
  Comparator #(.mode("unsigned")) comparator_3 (.a(RPH), .b(8'h1), .eq(comparator_3_eq));  // open: gt, lt
  RAM #(.addrWidth(16)) ram_1 (.addr({RPH, RPL}), .data(BUSH), .clk(and_14_out), .ld(and_15_out));  // open: sel, clr
  RAM #(.addrWidth(16)) ram_2 (.addr({RPH, RPL}), .data(BUSL), .clk(and_14_out), .ld(and_15_out));  // open: sel, clr
  Comparator #(.mode("unsigned")) comparator_4 (.a(RPL), .b({8{1'b0}}), .eq(comparator_4_eq));  // open: gt, lt
  Comparator #(.mode("unsigned")) comparator_5 (.a(RPH), .b(8'h2), .eq(comparator_5_eq));  // open: gt, lt
  Comparator #(.mode("unsigned")) comparator_6 (.a(RPL), .b({8{1'b0}}), .eq(comparator_6_eq));  // open: gt, lt
  assign BUSH = and_16_out ? button_1_out : 8'bz;  // Controlled_Buffer GPIAH
  assign BUSL = and_16_out ? joystick_1_y : 8'bz;  // Controlled_Buffer GPIAL
  and and_16 (and_16_out, comparator_3_eq, comparator_4_eq, BW_RAM);
  and and_17 (and_17_out, comparator_5_eq, comparator_6_eq, BR_RAM);
  Button button_1 (.out(button_1_out[0]));
  Button button_2 (.out(button_1_out[1]));
  Button button_3 (.out(button_1_out[2]));
  Button button_4 (.out(button_1_out[3]));
  Button button_5 (.out(button_1_out[4]));
  Button button_6 (.out(button_1_out[5]));
  Button button_7 (.out(button_1_out[6]));
  Button button_8 (.out(button_1_out[7]));
  Joystick joystick_1 (.x(joystick_1_y[7:4]), .y(joystick_1_y[3:0]));
  Register GPOAH (.D(BUSH), .en(and_17_out), .Q(GPOAH_q), .clk(CLK));  // open: clr
  LED led_1 (.in(GPOAH_q[0]));
  LED led_2 (.in(GPOAH_q[2]));
  LED led_3 (.in(GPOAH_q[4]));
  LED led_4 (.in(GPOAH_q[6]));
  Register GPOAL (.D(BUSL), .en(and_17_out), .Q(GPOAL_q), .clk(CLK));  // open: clr
  Hex_Digit_Display hex_digit_display_5 (.value(GPOAH_q[7:4]));  // open: dp
  LED led_5 (.in(GPOAH_q[1]));
  LED led_6 (.in(GPOAH_q[3]));
  LED led_7 (.in(GPOAH_q[5]));
  LED led_8 (.in(GPOAH_q[7]));
  _7_Segment_Display u_7_segment_display_1 (
    .g(GPOAL_q[6]), .f(GPOAL_q[5]), .a(GPOAL_q[0]), .b(GPOAL_q[1]), .e(GPOAL_q[4]), .d(GPOAL_q[3]),
    .c(GPOAL_q[2]), .dp(GPOAL_q[7]));
  Hex_Digit_Display hex_digit_display_6 (.value(GPOAL_q[7:4]));  // open: dp
  Hex_Digit_Display hex_digit_display_7 (.value(GPOAH_q[3:0]));  // open: dp
  Hex_Digit_Display hex_digit_display_8 (.value(GPOAL_q[3:0]));  // open: dp

  // Other names for the same wires on the sheet: NOR_C = BUSL[0]

  // Notes on the sheet:
  //   contents of rom_1 (hex, n*v repeats v):
  //   5 0 ff 4 fe ff 1 0 10 5 0 11 14 61 2 0 13 5 0 ff 45 a4 5 0 ff 42 1 ff ff a4 6 0 28 5 2 0 14 6 0 25
  //   61 2 0 13 5 0 ff 45 a4 5 0 ff 42 1 ff ff a4 6 0 56 5 0 11 41 a1 5 0 11 14 5 0 ff 42 1 0 1 a4 5 0 11
  //   41 5 0 ff 45 46 2 0 ff 5 0 12 24 5 0 ff 42 1 0 1 a4 5 0 12 42 5 0 ff 45 46 5 0 ff 42 1 0 1 a4 5 0 ff
  //   45 46
  //   0x0200
  //   0x0100
endmodule
