// Logisim project hera_logisim2.circ as structural Verilog: 13 circuits, main circuit main
module main (
);

  wire ADD_C, BR_A, BR_A_B, BR_A_D, BR_B, BR_B_D, BR_B_RP, BR_B_RP_t, BR_C, BR_C_D, BR_C_PC, BR_C_PC_t,
       BR_PC, BR_PC_C, BR_PC_D, BR_PC_D_t, BR_PC_N, BR_PC_t, BR_PC_Z, BR_RAM, BR_RAM_t, BR_RP, BR_RP_D,
       BR_STAT, BR_STAT_t, button_1_out, BW_A, BW_ADD, BW_B, BW_C, BW_COM, BW_LIT, BW_LIT_t, BW_NOR, BW_PC,
       BW_RAM, BW_RAM_t, BW_RP, BW_STAT, CLK, CLK2, COM_C, decoder_inv_2_1_d0, decoder_inv_2_1_d1,
       decoder_inv_2_1_d2, decoder_inv_2_1_d3, decoder_inv_4_1_d0, decoder_inv_4_1_d8, decoder_inv_4_1_d9,
       decoder_inv_4_1_d13, decoder_inv_4_1_d14, decoder_inv_4_1_d15, EN_BR, EN_BR_t, nand_1_out, nand_2_out,
       nand_3_out, nand_4_out, nand_5_out, nand_7_out, nand_8_out, nand_9_out, nand_10_out, nand_11_out,
       nand_12_out, nand_13_out, nand_14_out, nand_15_out, nor_1_out, nor_6_out, nor_7_out, nor_8_out,
       nor_10_out, nor_11_out, nor_12_out, nor_13_out, nor_14_out, nor_19_out, nor_20_out, nor_21_out,
       nor_22_out, nor_23_out, nor_24_out, nor_25_out, nor_31_out, nor_32_out, nor_33_out, nor_34_out,
       nor_35_out, not_8_out, not_11_out, not_12_out, not_13_out, not_20_out, not_21_out, not_23_out,
       not_25_out, not_26_out, not_27_out, not_28_out, not_29_out, not_30_out, not_31_out, not_32_out,
       not_33_out, register_1_1_q, RST, RST_IR_CNT, RST_t, xor_1_out;
  wire [1:0] counter_2_1_out_3;
  wire [3:0] nor_2_out, register_16_1_q_2, register_16_1_q_3;
  wire [7:0] BUSH, BUSL, IR1, IR1_t, IR2, IR2_t, IR3, IR3_t, register_16_1_q, rom_1_data;
  wire [15:0] A, A_t, adder_16_1_s, B, B_t, BUS, C, C_t, controlled_buffer_2_out, controlled_buffer_5_out,
       half_adder_16_1_s, half_adder_16_2_s, joystick_1_y, nor_26_out, nor_27_out, nor_28_out, nor_29_out,
       nor_30_out, PC, RP, RP_t, STAT, STAT_OW, STAT_t;

  Clock clock_1 (.out(CLK));
  Button button_1 (.out(button_1_out));
  not not_1 (RST, button_1_out);
  not not_2 (CLK2, CLK);
  not not_3 (RST_t, RST);
  counter_2 counter_2_1 (.RST(RST_IR_CNT), .CLK(CLK2), .out_3(counter_2_1_out_3));
  register_8 register_8_1 (.CLK(nor_1_out), .D(rom_1_data), .Q(IR1_t), .Q_2(IR1));
  nor nor_1 (nor_1_out, CLK2, decoder_inv_2_1_d0);
  decoder_inv_2 decoder_inv_2_1 (
    .D(counter_2_1_out_3), .D0(decoder_inv_2_1_d0), .D1(decoder_inv_2_1_d1), .D2(decoder_inv_2_1_d2),
    .D3(decoder_inv_2_1_d3));
  nor nor_2 (nor_2_out[0], IR1[0], EN_BR);
  nor nor_3 (nor_2_out[1], IR1[1], EN_BR);
  nor nor_4 (nor_2_out[2], IR1[2], EN_BR);
  nor nor_5 (nor_2_out[3], IR1[3], EN_BR);
  nor nor_6 (nor_6_out, BR_PC_N, STAT[2]);
  nor nor_7 (nor_7_out, BR_PC_Z, STAT[1]);
  nor nor_8 (nor_8_out, BR_PC_C, STAT[0]);
  decoder_inv_4 decoder_inv_4_1 (
    .D(IR1_t[7:4]), .D0(decoder_inv_4_1_d0), .D1(BW_A), .D2(BW_B), .D3(BW_C), .D4(BW_RAM), .D5(BW_RP),
    .D6(BW_PC), .D7(BW_STAT), .D8(decoder_inv_4_1_d8), .D9(decoder_inv_4_1_d9), .D10(BW_ADD), .D11(BW_COM),
    .D12(BW_NOR), .D13(decoder_inv_4_1_d13), .D14(decoder_inv_4_1_d14), .D15(decoder_inv_4_1_d15));
  decoder_inv_4 decoder_inv_4_2 (
    .D(nor_2_out), .D1(BR_A_D), .D2(BR_B_D), .D3(BR_C_D), .D4(BR_RAM), .D5(BR_RP_D), .D6(BR_PC_D),
    .D7(BR_STAT), .D10(BR_A_B), .D11(BR_B_RP), .D12(BR_C_PC), .D13(BR_PC_C), .D14(BR_PC_Z), .D15(BR_PC_N));  // open: D0, D8, D9
  nor nor_9 (BR_PC, BR_PC_D_t, BR_C_PC_t, nor_6_out, nor_7_out, nor_8_out);
  register_8 register_8_2 (.CLK(nor_10_out), .D(rom_1_data), .Q(IR2_t), .Q_2(IR2));
  nor nor_10 (nor_10_out, CLK2, decoder_inv_2_1_d1);
  not not_4 (BR_PC_t, BR_PC);
  ROM #(.addrWidth(16)) rom_1 (.addr(PC), .data(rom_1_data));  // open: sel
  register_8 register_8_3 (.CLK(nor_11_out), .D(rom_1_data), .Q(IR3_t), .Q_2(IR3));
  nor nor_11 (nor_11_out, CLK2, decoder_inv_2_1_d2);
  nor nor_12 (nor_12_out, decoder_inv_2_1_d2, BW_LIT_t);
  nor nor_13 (nor_13_out, decoder_inv_2_1_d1, BW_LIT_t);
  nor nor_14 (nor_14_out, decoder_inv_2_1_d3, BW_LIT);
  nand nand_1 (nand_1_out, BR_A_D, BR_A_B);
  not not_5 (BR_A, nand_1_out);
  nand nand_2 (nand_2_out, BR_B_D, BR_A_B);
  nor nor_15 (BR_B, nand_2_out, BR_B_RP_t);
  not not_6 (BR_RP, nand_3_out);
  nand nand_3 (nand_3_out, BR_RP_D, BR_B_RP);
  not not_7 (BR_C, nand_4_out);
  nand nand_4 (nand_4_out, BR_C_D, BR_C_PC);
  nor nor_16 (RST_IR_CNT, nor_12_out, RST_t);
  nor nor_17 (EN_BR, nor_13_out, nor_14_out);
  not not_8 (not_8_out, decoder_inv_4_1_d0);
  nor nor_18 (BW_LIT, not_8_out, nand_5_out);
  nand nand_5 (nand_5_out, decoder_inv_4_1_d8, decoder_inv_4_1_d9, decoder_inv_4_1_d13, decoder_inv_4_1_d14, decoder_inv_4_1_d15);
  not not_9 (EN_BR_t, EN_BR);
  not not_10 (BW_LIT_t, BW_LIT);
  not not_11 (not_11_out, ADD_C);
  not not_12 (not_12_out, COM_C);
  not not_13 (not_13_out, BUS[0]);
  Hex_Digit_Display hex_digit_display_1 (.value(BUSH[7:4]));  // open: dp
  Hex_Digit_Display hex_digit_display_2 (.value(BUSH[3:0]));  // open: dp
  nor nor_19 (nor_19_out, BUS[15], BUS[14], BUS[13], BUS[12]);
  nor nor_20 (nor_20_out, BUS[11], BUS[10], BUS[9], BUS[8]);
  nor nor_21 (nor_21_out, BUS[7], BUS[6], BUS[5], BUS[4]);
  nor nor_22 (nor_22_out, BUS[3], BUS[2], BUS[1], BUS[0]);
  nor nor_23 (nor_23_out, BW_ADD, not_11_out);
  nor nor_24 (nor_24_out, BW_COM, not_12_out);
  nor nor_25 (nor_25_out, BW_NOR, not_13_out);
  Hex_Digit_Display hex_digit_display_3 (.value(BUSL[3:0]));  // open: dp
  Hex_Digit_Display hex_digit_display_4 (.value(BUSL[7:4]));  // open: dp
  assign BUS = BW_LIT_t ? {IR2_t, IR3_t} : 16'bz;  // Controlled_Buffer controlled_buffer_1
  not not_14 (BW_RAM_t, BW_RAM);
  not not_15 (BR_RAM_t, BR_RAM);
  not not_16 (BR_PC_D_t, BR_PC_D);
  not not_17 (BR_STAT_t, BR_STAT);
  not not_18 (BR_B_RP_t, BR_B_RP);
  not not_19 (BR_C_PC_t, BR_C_PC);
  not not_20 (not_20_out, CLK);
  not not_21 (not_21_out, not_20_out);
  not not_22 (nor_26_out[2], BUS[15]);
  nand nand_6 (nor_26_out[1], nor_19_out, nor_20_out, nor_21_out, nor_22_out);
  nor nor_26 (nor_26_out[0], nor_23_out, nor_24_out, nor_25_out);
  register_bus_16 register_bus_16_1 (.CLK(CLK2), .BW(BW_A), .BR(BR_A), .BUS_IN(BUS), .Q(A_t), .Q_2(A), .BUS_OUT(BUS));
  register_bus_16 register_bus_16_2 (.CLK(CLK2), .BW(BW_B), .BR(BR_B), .BUS_IN(BUS), .Q(B_t), .Q_2(B), .BUS_OUT(BUS));
  register_bus_16 register_bus_16_3 (.CLK(CLK2), .BW(BW_C), .BR(BR_C), .BUS_IN(BUS), .Q(C_t), .Q_2(C), .BUS_OUT(BUS));
  register_bus_16 register_bus_16_4 (
    .CLK(CLK2), .BW(BW_RP), .BR(BR_RP), .BUS_IN(BUS), .Q(RP_t), .Q_2(RP), .BUS_OUT(BUS));
  nand nand_7 (nand_7_out, CLK, not_23_out);
  not not_23 (not_23_out, not_21_out);
  assign nor_27_out = ~(STAT | 16'h7);  // NOR_Gate nor_27, 16 bits wide
  assign nor_28_out = ~(nor_26_out | 16'hfff8);  // NOR_Gate nor_28, 16 bits wide
  assign controlled_buffer_2_out = RST_t ? {16{1'b0}} : 16'bz;  // Controlled_Buffer controlled_buffer_2
  assign STAT_OW = ~nor_29_out;  // NOT_Gate not_24, 16 bits wide
  assign nor_29_out = ~(nor_27_out | nor_28_out);  // NOR_Gate nor_29, 16 bits wide
  half_adder_16 half_adder_16_1 (.B(1'b1), .A(PC), .S(half_adder_16_1_s));  // open: C
  register_1 register_1_1 (.D(EN_BR_t), .Q(register_1_1_q), .READ(nand_7_out));  // open: Q_2
  nand nand_8 (nand_8_out, BR_STAT, BW_ADD, BW_COM, BW_NOR);
  adder_16 adder_16_1 (.C(1'b0), .B(B_t), .A(A_t), .S(adder_16_1_s), .C_2(ADD_C));
  half_adder_16 half_adder_16_2 (.B(1'b1), .C(COM_C), .A(A), .S(half_adder_16_2_s));
  assign controlled_buffer_2_out = not_25_out ? half_adder_16_1_s : 16'bz;  // Controlled_Buffer controlled_buffer_3
  nand nand_9 (nand_9_out, BR_PC, RST);
  not not_25 (not_25_out, nand_9_out);
  nand nand_10 (nand_10_out, register_1_1_q, BR_PC, RST);
  nand nand_11 (nand_11_out, nand_8_out, EN_BR_t);
  assign BUS = not_26_out ? nor_30_out : 16'bz;  // Controlled_Buffer controlled_buffer_4
  assign nor_30_out = ~(A_t | B_t);  // NOR_Gate nor_30, 16 bits wide
  not not_26 (not_26_out, BW_NOR);
  register_bus_16 register_bus_16_5 (
    .CLK(CLK), .BW(BW_PC), .BR(not_27_out), .BUS_IN(controlled_buffer_2_out), .Q(PC), .BUS_OUT(BUS));  // open: Q_2
  not not_27 (not_27_out, nand_10_out);
  assign controlled_buffer_5_out = BR_STAT ? STAT_OW : 16'bz;  // Controlled_Buffer controlled_buffer_5
  register_bus_16 register_bus_16_6 (
    .CLK(CLK2), .BW(BW_STAT), .BR(nand_11_out), .BUS_IN(controlled_buffer_5_out), .Q(STAT_t), .Q_2(STAT),
    .BUS_OUT(BUS));
  assign BUS = not_28_out ? adder_16_1_s : 16'bz;  // Controlled_Buffer controlled_buffer_6
  not not_28 (not_28_out, BW_ADD);
  assign BUS = not_29_out ? half_adder_16_2_s : 16'bz;  // Controlled_Buffer controlled_buffer_7
  not not_29 (not_29_out, BW_COM);
  assign controlled_buffer_2_out = not_30_out ? BUS : 16'bz;  // Controlled_Buffer controlled_buffer_8
  nand nand_12 (nand_12_out, BR_PC_t, RST);
  not not_30 (not_30_out, nand_12_out);
  assign controlled_buffer_5_out = BR_STAT_t ? BUS : 16'bz;  // Controlled_Buffer controlled_buffer_9
  nor nor_31 (nor_31_out, RP_t[15], RP_t[14], RP_t[13], RP_t[12], RP_t[11]);
  nor nor_32 (nor_32_out, BR_RAM, CLK2);
  nor nor_33 (nor_33_out, BW_RAM, RP_t[8]);
  nor nor_34 (nor_34_out, RP_t[10], RP_t[7], RP_t[6], RP_t[5], RP_t[4]);
  nor nor_35 (nor_35_out, RP_t[3], RP_t[2], RP_t[1], RP_t[0]);
  RAM #(.addrWidth(16)) ram_1 (.addr(RP_t), .data(BUS[15:8]), .clk(nor_32_out), .ld(nor_33_out));  // open: sel, clr
  RAM #(.addrWidth(16)) ram_2 (.addr(RP_t), .data(BUS[7:0]), .clk(nor_32_out), .ld(nor_33_out));  // open: sel, clr
  xor xor_1 (xor_1_out, RP_t[9], RP_t[8]);
  nand nand_13 (nand_13_out, xor_1_out, nor_31_out, nor_34_out, nor_35_out);
  not not_31 (not_31_out, nand_13_out);
  assign BUS = not_32_out ? joystick_1_y : 16'bz;  // Controlled_Buffer controlled_buffer_10
  not not_32 (not_32_out, nand_14_out);
  nand nand_14 (nand_14_out, RP_t[8], not_31_out, BW_RAM_t);
  register_16 register_16_1 (
    .CLK(not_33_out), .D(BUS), .Q({register_16_1_q_3, register_16_1_q_2, register_16_1_q}));  // open: Q_2
  nand nand_15 (nand_15_out, RP_t[9], not_31_out, CLK, BR_RAM_t);
  not not_33 (not_33_out, nand_15_out);
  Button button_2 (.out(joystick_1_y[8]));
  Button button_3 (.out(joystick_1_y[9]));
  Button button_4 (.out(joystick_1_y[10]));
  Button button_5 (.out(joystick_1_y[11]));
  Button button_6 (.out(joystick_1_y[12]));
  Button button_7 (.out(joystick_1_y[13]));
  Button button_8 (.out(joystick_1_y[14]));
  Button button_9 (.out(joystick_1_y[15]));
  Joystick joystick_1 (.x(joystick_1_y[7:4]), .y(joystick_1_y[3:0]));
  Hex_Digit_Display hex_digit_display_5 (.value(register_16_1_q_2));  // open: dp
  Hex_Digit_Display hex_digit_display_6 (.value(register_16_1_q_3));  // open: dp
  LED led_1 (.in(register_16_1_q_3[3]));
  LED led_2 (.in(register_16_1_q_3[1]));
  LED led_3 (.in(register_16_1_q_2[3]));
  LED led_4 (.in(register_16_1_q_2[1]));
  Hex_Digit_Display hex_digit_display_7 (.value(register_16_1_q[3:0]));  // open: dp
  Hex_Digit_Display hex_digit_display_8 (.value(register_16_1_q[7:4]));  // open: dp
  LED led_5 (.in(register_16_1_q_3[2]));
  LED led_6 (.in(register_16_1_q_3[0]));
  LED led_7 (.in(register_16_1_q_2[2]));
  LED led_8 (.in(register_16_1_q_2[0]));
  _7_Segment_Display u_7_segment_display_1 (
    .g(register_16_1_q[6]), .f(register_16_1_q[5]), .a(register_16_1_q[0]), .b(register_16_1_q[1]),
    .e(register_16_1_q[4]), .d(register_16_1_q[3]), .c(register_16_1_q[2]), .dp(register_16_1_q[7]));

  // Other names for the same wires on the sheet: NOR_C = BUS[0]

  // Notes on the sheet:
  //   DIFFERENCES:
  //   only inverting buffers
  //   BUF/#BUF
  //   separate CLK detector (register-8/16)
  //   contents of rom_1 (hex, n*v repeats v):
  //   1 0 1 b 0 80 4 0 3f ab 4 0 6 ab 4 0 5b ab 4 0 4f ab 4 0 66 ab 4 0 6d ab 4 0 7d ab 4 0 7 ab 4 0 7f ab
  //   4 0 6f ab 4 0 77 ab 4 0 7c ab 4 0 39 ab 4 0 5e ab 4 0 79 ab 4 0 71 5 1 0 4a c1 2 ff f0 c1 2 0 80 a5
  //   41 5 2 0 14 6 0 45
  //   better module blocks with in- & output pins -> connect as labels in main
  //   check if clk is pulsed by disabling gate at clk input
  //   dummy buffers with both pos/neg inputs
  //   0x0100 (GPIA)
  //   0x0200 (GPOA)
endmodule

module decoder_inv_2 (
  input  [1:0] D,
  output D0,
  output D1,
  output D2,
  output D3
);

  wire not_1_out, not_2_out;

  not not_1 (not_1_out, D[1]);
  not not_2 (not_2_out, D[0]);
  nand nand_1 (D0, not_2_out, not_1_out);
  nand nand_2 (D1, D[0], not_1_out);
  nand nand_3 (D2, not_2_out, D[1]);
  nand nand_4 (D3, D[0], D[1]);
endmodule

module decoder_4 (
  input  [3:0] D,
  output D0,
  output D1,
  output D2,
  output D3,
  output D4,
  output D5,
  output D6,
  output D7,
  output D8,
  output D9,
  output D10,
  output D11,
  output D12,
  output D13,
  output D14,
  output D15
);

  wire not_1_out, not_2_out, not_3_out, not_4_out;

  not not_1 (not_1_out, D[3]);
  not not_2 (not_2_out, D[2]);
  not not_3 (not_3_out, D[1]);
  not not_4 (not_4_out, D[0]);
  and and_1 (D0, not_4_out, not_3_out, not_2_out, not_1_out);
  and and_2 (D1, D[0], not_3_out, not_2_out, not_1_out);
  and and_3 (D2, not_4_out, D[1], not_2_out, not_1_out);
  and and_4 (D3, D[0], D[1], not_2_out, not_1_out);
  and and_5 (D4, not_4_out, not_3_out, D[2], not_1_out);
  and and_6 (D5, D[0], not_3_out, D[2], not_1_out);
  and and_7 (D6, not_4_out, D[1], D[2], not_1_out);
  and and_8 (D7, D[0], D[1], D[2], not_1_out);
  and and_9 (D8, not_4_out, not_3_out, not_2_out, D[3]);
  and and_10 (D9, D[0], not_3_out, not_2_out, D[3]);
  and and_11 (D10, not_4_out, D[1], not_2_out, D[3]);
  and and_12 (D11, D[0], D[1], not_2_out, D[3]);
  and and_13 (D12, not_4_out, not_3_out, D[2], D[3]);
  and and_14 (D13, D[0], not_3_out, D[2], D[3]);
  and and_15 (D14, not_4_out, D[1], D[2], D[3]);
  and and_16 (D15, D[0], D[1], D[2], D[3]);
endmodule

module decoder_inv_4 (
  input  [3:0] D,
  output D0,
  output D1,
  output D2,
  output D3,
  output D4,
  output D5,
  output D6,
  output D7,
  output D8,
  output D9,
  output D10,
  output D11,
  output D12,
  output D13,
  output D14,
  output D15
);

  wire not_1_out, not_2_out, not_3_out, not_4_out;

  not not_1 (not_1_out, D[3]);
  not not_2 (not_2_out, D[2]);
  not not_3 (not_3_out, D[1]);
  not not_4 (not_4_out, D[0]);
  nand nand_1 (D0, not_4_out, not_3_out, not_2_out, not_1_out);
  nand nand_2 (D1, D[0], not_3_out, not_2_out, not_1_out);
  nand nand_3 (D2, not_4_out, D[1], not_2_out, not_1_out);
  nand nand_4 (D3, D[0], D[1], not_2_out, not_1_out);
  nand nand_5 (D4, not_4_out, not_3_out, D[2], not_1_out);
  nand nand_6 (D5, D[0], not_3_out, D[2], not_1_out);
  nand nand_7 (D6, not_4_out, D[1], D[2], not_1_out);
  nand nand_8 (D7, D[0], D[1], D[2], not_1_out);
  nand nand_9 (D8, not_4_out, not_3_out, not_2_out, D[3]);
  nand nand_10 (D9, D[0], not_3_out, not_2_out, D[3]);
  nand nand_11 (D10, not_4_out, D[1], not_2_out, D[3]);
  nand nand_12 (D11, D[0], D[1], not_2_out, D[3]);
  nand nand_13 (D12, not_4_out, not_3_out, D[2], D[3]);
  nand nand_14 (D13, D[0], not_3_out, D[2], D[3]);
  nand nand_15 (D14, not_4_out, D[1], D[2], D[3]);
  nand nand_16 (D15, D[0], D[1], D[2], D[3]);
endmodule

module register_1 (
  input  D,
  input  READ,
  output Q,
  output Q_2
);

  wire nor_1_out, nor_2_out, not_1_out;

  nor nor_1 (nor_1_out, D, READ);
  not not_1 (not_1_out, D);
  nor nor_2 (nor_2_out, not_1_out, READ);
  nor nor_3 (Q, nor_1_out, Q_2);
  nor nor_4 (Q_2, Q, nor_2_out);
endmodule

module register_8 (
  input  [7:0] D,
  input  CLK,
  output [7:0] Q,
  output [7:0] Q_2
);

  wire nand_1_out, not_1_out, not_2_out, not_3_out;

  not not_1 (not_1_out, CLK);
  not not_2 (not_2_out, not_1_out);
  nand nand_1 (nand_1_out, CLK, not_3_out);
  not not_3 (not_3_out, not_2_out);
  register_1 register_1_1 (.D(D[0]), .Q(Q[0]), .Q_2(Q_2[0]), .READ(nand_1_out));
  register_1 register_1_2 (.D(D[1]), .Q(Q[1]), .Q_2(Q_2[1]), .READ(nand_1_out));
  register_1 register_1_3 (.D(D[2]), .Q(Q[2]), .Q_2(Q_2[2]), .READ(nand_1_out));
  register_1 register_1_4 (.D(D[3]), .Q(Q[3]), .Q_2(Q_2[3]), .READ(nand_1_out));
  register_1 register_1_5 (.D(D[4]), .Q(Q[4]), .Q_2(Q_2[4]), .READ(nand_1_out));
  register_1 register_1_6 (.D(D[5]), .Q(Q[5]), .Q_2(Q_2[5]), .READ(nand_1_out));
  register_1 register_1_7 (.D(D[6]), .Q(Q[6]), .Q_2(Q_2[6]), .READ(nand_1_out));
  register_1 register_1_8 (.D(D[7]), .Q(Q[7]), .Q_2(Q_2[7]), .READ(nand_1_out));
endmodule

module register_16 (
  input  [15:0] D,
  input  CLK,
  output [15:0] Q,
  output [15:0] Q_2
);

  wire nand_1_out, not_1_out, not_2_out, not_3_out;

  not not_1 (not_1_out, CLK);
  not not_2 (not_2_out, not_1_out);
  nand nand_1 (nand_1_out, CLK, not_3_out);
  not not_3 (not_3_out, not_2_out);
  register_1 register_1_1 (.D(D[0]), .Q(Q[0]), .Q_2(Q_2[0]), .READ(nand_1_out));
  register_1 register_1_2 (.D(D[1]), .Q(Q[1]), .Q_2(Q_2[1]), .READ(nand_1_out));
  register_1 register_1_3 (.D(D[2]), .Q(Q[2]), .Q_2(Q_2[2]), .READ(nand_1_out));
  register_1 register_1_4 (.D(D[3]), .Q(Q[3]), .Q_2(Q_2[3]), .READ(nand_1_out));
  register_1 register_1_5 (.D(D[4]), .Q(Q[4]), .Q_2(Q_2[4]), .READ(nand_1_out));
  register_1 register_1_6 (.D(D[5]), .Q(Q[5]), .Q_2(Q_2[5]), .READ(nand_1_out));
  register_1 register_1_7 (.D(D[6]), .Q(Q[6]), .Q_2(Q_2[6]), .READ(nand_1_out));
  register_1 register_1_8 (.D(D[7]), .Q(Q[7]), .Q_2(Q_2[7]), .READ(nand_1_out));
  register_1 register_1_9 (.D(D[8]), .Q(Q[8]), .Q_2(Q_2[8]), .READ(nand_1_out));
  register_1 register_1_10 (.D(D[9]), .Q(Q[9]), .Q_2(Q_2[9]), .READ(nand_1_out));
  register_1 register_1_11 (.D(D[10]), .Q(Q[10]), .Q_2(Q_2[10]), .READ(nand_1_out));
  register_1 register_1_12 (.D(D[11]), .Q(Q[11]), .Q_2(Q_2[11]), .READ(nand_1_out));
  register_1 register_1_13 (.D(D[12]), .Q(Q[12]), .Q_2(Q_2[12]), .READ(nand_1_out));
  register_1 register_1_14 (.D(D[13]), .Q(Q[13]), .Q_2(Q_2[13]), .READ(nand_1_out));
  register_1 register_1_15 (.D(D[14]), .Q(Q[14]), .Q_2(Q_2[14]), .READ(nand_1_out));
  register_1 register_1_16 (.D(D[15]), .Q(Q[15]), .Q_2(Q_2[15]), .READ(nand_1_out));
endmodule

module register_bus_16 (
  input  [15:0] BUS_IN,
  input  BW,
  input  CLK,
  input  BR,
  output [15:0] Q,
  output [15:0] BUS_OUT,
  output [15:0] Q_2
);

  wire nor_1_out, not_1_out;

  register_16 register_16_1 (.CLK(nor_1_out), .D(BUS_IN), .Q(Q), .Q_2(Q_2));
  nor nor_1 (nor_1_out, CLK, BR);
  assign BUS_OUT = not_1_out ? Q : 16'bz;  // Controlled_Buffer controlled_buffer_1
  not not_1 (not_1_out, BW);
endmodule

module adder_1 (
  input  A,
  input  B,
  input  C,
  output S,
  output C_2
);

  wire nand_1_out, nand_2_out, xor_1_out;

  xor xor_1 (xor_1_out, A, B);
  xor xor_2 (S, xor_1_out, C);
  nand nand_1 (nand_1_out, C, xor_1_out);
  nand nand_2 (nand_2_out, A, B);
  nand nand_3 (C_2, nand_1_out, nand_2_out);
endmodule

module adder_16 (
  input  [15:0] B,
  input  [15:0] A,
  input  C,
  output [15:0] S,
  output C_2
);

  wire adder_1_1_c_2, adder_1_2_c_2, adder_1_3_c_2, adder_1_4_c_2, adder_1_5_c_2, adder_1_6_c_2,
       adder_1_7_c_2, adder_1_8_c_2, adder_1_9_c_2, adder_1_10_c_2, adder_1_11_c_2, adder_1_12_c_2,
       adder_1_13_c_2, adder_1_14_c_2, adder_1_15_c_2;

  adder_1 adder_1_1 (.A(A[0]), .B(B[0]), .C(C), .S(S[0]), .C_2(adder_1_1_c_2));
  adder_1 adder_1_2 (.A(A[1]), .B(B[1]), .C(adder_1_1_c_2), .S(S[1]), .C_2(adder_1_2_c_2));
  adder_1 adder_1_3 (.A(A[2]), .B(B[2]), .C(adder_1_2_c_2), .S(S[2]), .C_2(adder_1_3_c_2));
  adder_1 adder_1_4 (.A(A[3]), .B(B[3]), .C(adder_1_3_c_2), .S(S[3]), .C_2(adder_1_4_c_2));
  adder_1 adder_1_5 (.A(A[4]), .B(B[4]), .C(adder_1_4_c_2), .S(S[4]), .C_2(adder_1_5_c_2));
  adder_1 adder_1_6 (.A(A[5]), .B(B[5]), .C(adder_1_5_c_2), .S(S[5]), .C_2(adder_1_6_c_2));
  adder_1 adder_1_7 (.A(A[6]), .B(B[6]), .C(adder_1_6_c_2), .S(S[6]), .C_2(adder_1_7_c_2));
  adder_1 adder_1_8 (.A(A[7]), .B(B[7]), .C(adder_1_7_c_2), .S(S[7]), .C_2(adder_1_8_c_2));
  adder_1 adder_1_9 (.A(A[8]), .B(B[8]), .C(adder_1_8_c_2), .S(S[8]), .C_2(adder_1_9_c_2));
  adder_1 adder_1_10 (.A(A[9]), .B(B[9]), .C(adder_1_9_c_2), .S(S[9]), .C_2(adder_1_10_c_2));
  adder_1 adder_1_11 (.A(A[10]), .B(B[10]), .C(adder_1_10_c_2), .S(S[10]), .C_2(adder_1_11_c_2));
  adder_1 adder_1_12 (.A(A[11]), .B(B[11]), .C(adder_1_11_c_2), .S(S[11]), .C_2(adder_1_12_c_2));
  adder_1 adder_1_13 (.A(A[12]), .B(B[12]), .C(adder_1_12_c_2), .S(S[12]), .C_2(adder_1_13_c_2));
  adder_1 adder_1_14 (.A(A[13]), .B(B[13]), .C(adder_1_13_c_2), .S(S[13]), .C_2(adder_1_14_c_2));
  adder_1 adder_1_15 (.A(A[14]), .B(B[14]), .C(adder_1_14_c_2), .S(S[14]), .C_2(adder_1_15_c_2));
  adder_1 adder_1_16 (.A(A[15]), .B(B[15]), .C(adder_1_15_c_2), .S(S[15]), .C_2(C_2));
endmodule

module half_adder_1 (
  input  A,
  input  B,
  output S,
  output C
);

  xor xor_1 (S, A, B);
  and and_1 (C, A, B);
endmodule

module half_adder_16 (
  input  [15:0] A,
  input  B,
  output [15:0] S,
  output C
);

  wire half_adder_1_1_c, half_adder_1_2_c, half_adder_1_3_c, half_adder_1_4_c, half_adder_1_5_c,
       half_adder_1_6_c, half_adder_1_7_c, half_adder_1_8_c, half_adder_1_9_c, half_adder_1_10_c,
       half_adder_1_11_c, half_adder_1_12_c, half_adder_1_13_c, half_adder_1_14_c, half_adder_1_15_c;

  half_adder_1 half_adder_1_1 (.A(A[0]), .B(B), .S(S[0]), .C(half_adder_1_1_c));
  half_adder_1 half_adder_1_2 (.A(A[1]), .B(half_adder_1_1_c), .S(S[1]), .C(half_adder_1_2_c));
  half_adder_1 half_adder_1_3 (.A(A[2]), .B(half_adder_1_2_c), .S(S[2]), .C(half_adder_1_3_c));
  half_adder_1 half_adder_1_4 (.A(A[3]), .B(half_adder_1_3_c), .S(S[3]), .C(half_adder_1_4_c));
  half_adder_1 half_adder_1_5 (.A(A[4]), .B(half_adder_1_4_c), .S(S[4]), .C(half_adder_1_5_c));
  half_adder_1 half_adder_1_6 (.A(A[5]), .B(half_adder_1_5_c), .S(S[5]), .C(half_adder_1_6_c));
  half_adder_1 half_adder_1_7 (.A(A[6]), .B(half_adder_1_6_c), .S(S[6]), .C(half_adder_1_7_c));
  half_adder_1 half_adder_1_8 (.A(A[7]), .B(half_adder_1_7_c), .S(S[7]), .C(half_adder_1_8_c));
  half_adder_1 half_adder_1_9 (.A(A[8]), .B(half_adder_1_8_c), .S(S[8]), .C(half_adder_1_9_c));
  half_adder_1 half_adder_1_10 (.A(A[9]), .B(half_adder_1_9_c), .S(S[9]), .C(half_adder_1_10_c));
  half_adder_1 half_adder_1_11 (.A(A[10]), .B(half_adder_1_10_c), .S(S[10]), .C(half_adder_1_11_c));
  half_adder_1 half_adder_1_12 (.A(A[11]), .B(half_adder_1_11_c), .S(S[11]), .C(half_adder_1_12_c));
  half_adder_1 half_adder_1_13 (.A(A[12]), .B(half_adder_1_12_c), .S(S[12]), .C(half_adder_1_13_c));
  half_adder_1 half_adder_1_14 (.A(A[13]), .B(half_adder_1_13_c), .S(S[13]), .C(half_adder_1_14_c));
  half_adder_1 half_adder_1_15 (.A(A[14]), .B(half_adder_1_14_c), .S(S[14]), .C(half_adder_1_15_c));
  half_adder_1 half_adder_1_16 (.A(A[15]), .B(half_adder_1_15_c), .S(S[15]), .C(C));
endmodule

module counter_2 (
  input  RST,
  input  CLK,
  output [1:0] out_3
);

  wire and_1_out, and_2_out, and_3_out, and_4_out, and_5_out, nand_1_out, nand_2_out, not_1_out, not_2_out,
       not_3_out, not_4_out, not_5_out, not_6_out, not_7_out, not_8_out, register_1_3_q, register_1_4_q,
       xor_1_out, xor_2_out;

  not not_1 (not_1_out, not_2_out);
  not not_2 (not_2_out, CLK);
  not not_3 (not_3_out, not_1_out);
  not not_4 (not_4_out, not_5_out);
  not not_5 (not_5_out, CLK);
  not not_6 (not_6_out, not_4_out);
  and and_1 (and_1_out, RST, nand_1_out);
  nand nand_1 (nand_1_out, CLK, not_3_out);
  not not_7 (not_7_out, CLK);
  nand nand_2 (nand_2_out, not_7_out, not_8_out);
  not not_8 (not_8_out, not_6_out);
  and and_2 (and_2_out, register_1_3_q, RST);
  and and_3 (and_3_out, register_1_4_q, RST);
  and and_4 (and_4_out, RST, nand_2_out);
  register_1 register_1_1 (.D(and_2_out), .Q(out_3[0]), .READ(and_1_out));  // open: Q_2
  register_1 register_1_2 (.D(and_3_out), .Q(out_3[1]), .READ(and_1_out));  // open: Q_2
  xor xor_1 (xor_1_out, out_3[0], 1'b1);
  and and_5 (and_5_out, out_3[0], 1'b1);
  xor xor_2 (xor_2_out, out_3[1], and_5_out);
  register_1 register_1_3 (.D(xor_1_out), .Q(register_1_3_q), .READ(and_4_out));  // open: Q_2
  register_1 register_1_4 (.D(xor_2_out), .Q(register_1_4_q), .READ(and_4_out));  // open: Q_2
endmodule
