// Logisim project hera_logisim3.circ as structural Verilog: 17 circuits, main circuit main
module main (
);

  wire button_1_out, clock_1_out, mod_1_rom_1_en_br, STAT_C, STAT_N, STAT_Z;
  wire [7:0] IR;
  wire [15:0] BUS;

  Clock clock_1 (.out(clock_1_out));
  Button button_1 (.out(button_1_out));
  mod_1_rom mod_1_rom_1 (
    .CLK(clock_1_out), .STAT_N(STAT_N), .STAT_Z(STAT_Z), .STAT_C(STAT_C), .BUS_IN(BUS), .RST(button_1_out),
    .IR(IR), .BUS_OUT(BUS), .EN_BR(mod_1_rom_1_en_br));
  mod_2_alu mod_2_alu_1 (
    .CLK(clock_1_out), .BUS_IN(BUS), .IR(IR), .STAT_N(STAT_N), .STAT_Z(STAT_Z), .STAT_C(STAT_C),
    .BUS_OUT(BUS), .EN_BR(mod_1_rom_1_en_br));
  mod_3_c mod_3_c_1 (.IR(IR), .CLK(clock_1_out), .BUS_IN(BUS), .BUS_OUT(BUS));
  mod_4_ram mod_4_ram_1 (.CLK(clock_1_out), .BUS_IN(BUS), .IR(IR), .BUS_OUT(BUS));
  Hex_Digit_Display hex_digit_display_1 (.value(BUS[11:8]));  // open: dp
  Hex_Digit_Display hex_digit_display_2 (.value(BUS[15:12]));  // open: dp
  Hex_Digit_Display hex_digit_display_3 (.value(BUS[7:4]));  // open: dp
  Hex_Digit_Display hex_digit_display_4 (.value(BUS[3:0]));  // open: dp

  // Notes on the sheet:
  //   DIFFERENCES:
  //   only inverting buffers
  //   BUF/#BUF
  //   separate CLK edge detector (register-8/16)
  //   dummy buffers with both pos/neg inputs
  //   check if clk is pulsed by disabling gate at clk input
endmodule

module decoder_inv_2 (
  input  [1:0] D,
  output D0,
  output D1,
  output D2,
  output D3
);

  wire not_1_out, not_2_out;

  not not_1 (not_1_out, D[1]);
  not not_2 (not_2_out, D[0]);
  nand nand_1 (D0, not_2_out, not_1_out);
  nand nand_2 (D1, D[0], not_1_out);
  nand nand_3 (D2, not_2_out, D[1]);
  nand nand_4 (D3, D[0], D[1]);
endmodule

module decoder_4 (
  input  [3:0] D,
  output D0,
  output D1,
  output D2,
  output D3,
  output D4,
  output D5,
  output D6,
  output D7,
  output D8,
  output D9,
  output D10,
  output D11,
  output D12,
  output D13,
  output D14,
  output D15
);

  wire not_1_out, not_2_out, not_3_out, not_4_out;

  not not_1 (not_1_out, D[3]);
  not not_2 (not_2_out, D[2]);
  not not_3 (not_3_out, D[1]);
  not not_4 (not_4_out, D[0]);
  and and_1 (D0, not_4_out, not_3_out, not_2_out, not_1_out);
  and and_2 (D1, D[0], not_3_out, not_2_out, not_1_out);
  and and_3 (D2, not_4_out, D[1], not_2_out, not_1_out);
  and and_4 (D3, D[0], D[1], not_2_out, not_1_out);
  and and_5 (D4, not_4_out, not_3_out, D[2], not_1_out);
  and and_6 (D5, D[0], not_3_out, D[2], not_1_out);
  and and_7 (D6, not_4_out, D[1], D[2], not_1_out);
  and and_8 (D7, D[0], D[1], D[2], not_1_out);
  and and_9 (D8, not_4_out, not_3_out, not_2_out, D[3]);
  and and_10 (D9, D[0], not_3_out, not_2_out, D[3]);
  and and_11 (D10, not_4_out, D[1], not_2_out, D[3]);
  and and_12 (D11, D[0], D[1], not_2_out, D[3]);
  and and_13 (D12, not_4_out, not_3_out, D[2], D[3]);
  and and_14 (D13, D[0], not_3_out, D[2], D[3]);
  and and_15 (D14, not_4_out, D[1], D[2], D[3]);
  and and_16 (D15, D[0], D[1], D[2], D[3]);
endmodule

module decoder_inv_4 (
  input  [3:0] D,
  output D0,
  output D1,
  output D2,
  output D3,
  output D4,
  output D5,
  output D6,
  output D7,
  output D8,
  output D9,
  output D10,
  output D11,
  output D12,
  output D13,
  output D14,
  output D15
);

  wire not_1_out, not_2_out, not_3_out, not_4_out;

  not not_1 (not_1_out, D[3]);
  not not_2 (not_2_out, D[2]);
  not not_3 (not_3_out, D[1]);
  not not_4 (not_4_out, D[0]);
  nand nand_1 (D0, not_4_out, not_3_out, not_2_out, not_1_out);
  nand nand_2 (D1, D[0], not_3_out, not_2_out, not_1_out);
  nand nand_3 (D2, not_4_out, D[1], not_2_out, not_1_out);
  nand nand_4 (D3, D[0], D[1], not_2_out, not_1_out);
  nand nand_5 (D4, not_4_out, not_3_out, D[2], not_1_out);
  nand nand_6 (D5, D[0], not_3_out, D[2], not_1_out);
  nand nand_7 (D6, not_4_out, D[1], D[2], not_1_out);
  nand nand_8 (D7, D[0], D[1], D[2], not_1_out);
  nand nand_9 (D8, not_4_out, not_3_out, not_2_out, D[3]);
  nand nand_10 (D9, D[0], not_3_out, not_2_out, D[3]);
  nand nand_11 (D10, not_4_out, D[1], not_2_out, D[3]);
  nand nand_12 (D11, D[0], D[1], not_2_out, D[3]);
  nand nand_13 (D12, not_4_out, not_3_out, D[2], D[3]);
  nand nand_14 (D13, D[0], not_3_out, D[2], D[3]);
  nand nand_15 (D14, not_4_out, D[1], D[2], D[3]);
  nand nand_16 (D15, D[0], D[1], D[2], D[3]);
endmodule

module register_1 (
  input  D,
  input  READ,
  output Q,
  output Q_2
);

  wire nor_1_out, nor_2_out, not_1_out;

  nor nor_1 (nor_1_out, D, READ);
  not not_1 (not_1_out, D);
  nor nor_2 (nor_2_out, not_1_out, READ);
  nor nor_3 (Q, nor_1_out, Q_2);
  nor nor_4 (Q_2, Q, nor_2_out);
endmodule

module register_8 (
  input  [7:0] D,
  input  CLK,
  output [7:0] Q,
  output [7:0] Q_2
);

  wire nand_1_out, not_1_out, not_2_out, not_3_out;

  not not_1 (not_1_out, not_2_out);
  not not_2 (not_2_out, CLK);
  nand nand_1 (nand_1_out, CLK, not_3_out);
  not not_3 (not_3_out, not_1_out);
  register_1 register_1_1 (.D(D[0]), .Q(Q[0]), .Q_2(Q_2[0]), .READ(nand_1_out));
  register_1 register_1_2 (.D(D[1]), .Q(Q[1]), .Q_2(Q_2[1]), .READ(nand_1_out));
  register_1 register_1_3 (.D(D[2]), .Q(Q[2]), .Q_2(Q_2[2]), .READ(nand_1_out));
  register_1 register_1_4 (.D(D[3]), .Q(Q[3]), .Q_2(Q_2[3]), .READ(nand_1_out));
  register_1 register_1_5 (.D(D[4]), .Q(Q[4]), .Q_2(Q_2[4]), .READ(nand_1_out));
  register_1 register_1_6 (.D(D[5]), .Q(Q[5]), .Q_2(Q_2[5]), .READ(nand_1_out));
  register_1 register_1_7 (.D(D[6]), .Q(Q[6]), .Q_2(Q_2[6]), .READ(nand_1_out));
  register_1 register_1_8 (.D(D[7]), .Q(Q[7]), .Q_2(Q_2[7]), .READ(nand_1_out));
endmodule

module register_16 (
  input  [15:0] D,
  input  CLK,
  output [15:0] Q,
  output [15:0] Q_2
);

  wire nand_1_out, not_1_out, not_2_out, not_3_out;

  not not_1 (not_1_out, CLK);
  not not_2 (not_2_out, not_1_out);
  nand nand_1 (nand_1_out, CLK, not_3_out);
  not not_3 (not_3_out, not_2_out);
  register_1 register_1_1 (.D(D[0]), .Q(Q[0]), .Q_2(Q_2[0]), .READ(nand_1_out));
  register_1 register_1_2 (.D(D[1]), .Q(Q[1]), .Q_2(Q_2[1]), .READ(nand_1_out));
  register_1 register_1_3 (.D(D[2]), .Q(Q[2]), .Q_2(Q_2[2]), .READ(nand_1_out));
  register_1 register_1_4 (.D(D[3]), .Q(Q[3]), .Q_2(Q_2[3]), .READ(nand_1_out));
  register_1 register_1_5 (.D(D[4]), .Q(Q[4]), .Q_2(Q_2[4]), .READ(nand_1_out));
  register_1 register_1_6 (.D(D[5]), .Q(Q[5]), .Q_2(Q_2[5]), .READ(nand_1_out));
  register_1 register_1_7 (.D(D[6]), .Q(Q[6]), .Q_2(Q_2[6]), .READ(nand_1_out));
  register_1 register_1_8 (.D(D[7]), .Q(Q[7]), .Q_2(Q_2[7]), .READ(nand_1_out));
  register_1 register_1_9 (.D(D[8]), .Q(Q[8]), .Q_2(Q_2[8]), .READ(nand_1_out));
  register_1 register_1_10 (.D(D[9]), .Q(Q[9]), .Q_2(Q_2[9]), .READ(nand_1_out));
  register_1 register_1_11 (.D(D[10]), .Q(Q[10]), .Q_2(Q_2[10]), .READ(nand_1_out));
  register_1 register_1_12 (.D(D[11]), .Q(Q[11]), .Q_2(Q_2[11]), .READ(nand_1_out));
  register_1 register_1_13 (.D(D[12]), .Q(Q[12]), .Q_2(Q_2[12]), .READ(nand_1_out));
  register_1 register_1_14 (.D(D[13]), .Q(Q[13]), .Q_2(Q_2[13]), .READ(nand_1_out));
  register_1 register_1_15 (.D(D[14]), .Q(Q[14]), .Q_2(Q_2[14]), .READ(nand_1_out));
  register_1 register_1_16 (.D(D[15]), .Q(Q[15]), .Q_2(Q_2[15]), .READ(nand_1_out));
endmodule

module register_bus_16 (
  input  [15:0] BUS_IN,
  input  BW,
  input  CLK,
  input  BR,
  output [15:0] Q,
  output [15:0] BUS_OUT,
  output [15:0] Q_2
);

  wire nor_1_out, not_1_out;

  register_16 register_16_1 (.CLK(nor_1_out), .D(BUS_IN), .Q(Q), .Q_2(Q_2));
  nor nor_1 (nor_1_out, CLK, BR);
  assign BUS_OUT = not_1_out ? Q : 16'bz;  // Controlled_Buffer controlled_buffer_1
  not not_1 (not_1_out, BW);
endmodule

module adder_1 (
  input  A,
  input  B,
  input  C,
  output S,
  output C_2
);

  wire nand_1_out, nand_2_out, xor_1_out;

  xor xor_1 (xor_1_out, A, B);
  xor xor_2 (S, xor_1_out, C);
  nand nand_1 (nand_1_out, C, xor_1_out);
  nand nand_2 (nand_2_out, A, B);
  nand nand_3 (C_2, nand_1_out, nand_2_out);
endmodule

module adder_16 (
  input  [15:0] B,
  input  [15:0] A,
  input  C,
  output [15:0] S,
  output C_2
);

  wire adder_1_1_c_2, adder_1_2_c_2, adder_1_3_c_2, adder_1_4_c_2, adder_1_5_c_2, adder_1_6_c_2,
       adder_1_7_c_2, adder_1_8_c_2, adder_1_9_c_2, adder_1_10_c_2, adder_1_11_c_2, adder_1_12_c_2,
       adder_1_13_c_2, adder_1_14_c_2, adder_1_15_c_2;

  adder_1 adder_1_1 (.A(A[0]), .B(B[0]), .C(C), .S(S[0]), .C_2(adder_1_1_c_2));
  adder_1 adder_1_2 (.A(A[1]), .B(B[1]), .C(adder_1_1_c_2), .S(S[1]), .C_2(adder_1_2_c_2));
  adder_1 adder_1_3 (.A(A[2]), .B(B[2]), .C(adder_1_2_c_2), .S(S[2]), .C_2(adder_1_3_c_2));
  adder_1 adder_1_4 (.A(A[3]), .B(B[3]), .C(adder_1_3_c_2), .S(S[3]), .C_2(adder_1_4_c_2));
  adder_1 adder_1_5 (.A(A[4]), .B(B[4]), .C(adder_1_4_c_2), .S(S[4]), .C_2(adder_1_5_c_2));
  adder_1 adder_1_6 (.A(A[5]), .B(B[5]), .C(adder_1_5_c_2), .S(S[5]), .C_2(adder_1_6_c_2));
  adder_1 adder_1_7 (.A(A[6]), .B(B[6]), .C(adder_1_6_c_2), .S(S[6]), .C_2(adder_1_7_c_2));
  adder_1 adder_1_8 (.A(A[7]), .B(B[7]), .C(adder_1_7_c_2), .S(S[7]), .C_2(adder_1_8_c_2));
  adder_1 adder_1_9 (.A(A[8]), .B(B[8]), .C(adder_1_8_c_2), .S(S[8]), .C_2(adder_1_9_c_2));
  adder_1 adder_1_10 (.A(A[9]), .B(B[9]), .C(adder_1_9_c_2), .S(S[9]), .C_2(adder_1_10_c_2));
  adder_1 adder_1_11 (.A(A[10]), .B(B[10]), .C(adder_1_10_c_2), .S(S[10]), .C_2(adder_1_11_c_2));
  adder_1 adder_1_12 (.A(A[11]), .B(B[11]), .C(adder_1_11_c_2), .S(S[11]), .C_2(adder_1_12_c_2));
  adder_1 adder_1_13 (.A(A[12]), .B(B[12]), .C(adder_1_12_c_2), .S(S[12]), .C_2(adder_1_13_c_2));
  adder_1 adder_1_14 (.A(A[13]), .B(B[13]), .C(adder_1_13_c_2), .S(S[13]), .C_2(adder_1_14_c_2));
  adder_1 adder_1_15 (.A(A[14]), .B(B[14]), .C(adder_1_14_c_2), .S(S[14]), .C_2(adder_1_15_c_2));
  adder_1 adder_1_16 (.A(A[15]), .B(B[15]), .C(adder_1_15_c_2), .S(S[15]), .C_2(C_2));
endmodule

module half_adder_1 (
  input  A,
  input  B,
  output S,
  output C
);

  xor xor_1 (S, A, B);
  and and_1 (C, A, B);
endmodule

module half_adder_16 (
  input  [15:0] A,
  input  B,
  output [15:0] S,
  output C
);

  wire half_adder_1_1_c, half_adder_1_2_c, half_adder_1_3_c, half_adder_1_4_c, half_adder_1_5_c,
       half_adder_1_6_c, half_adder_1_7_c, half_adder_1_8_c, half_adder_1_9_c, half_adder_1_10_c,
       half_adder_1_11_c, half_adder_1_12_c, half_adder_1_13_c, half_adder_1_14_c, half_adder_1_15_c;

  half_adder_1 half_adder_1_1 (.A(A[0]), .B(B), .S(S[0]), .C(half_adder_1_1_c));
  half_adder_1 half_adder_1_2 (.A(A[1]), .B(half_adder_1_1_c), .S(S[1]), .C(half_adder_1_2_c));
  half_adder_1 half_adder_1_3 (.A(A[2]), .B(half_adder_1_2_c), .S(S[2]), .C(half_adder_1_3_c));
  half_adder_1 half_adder_1_4 (.A(A[3]), .B(half_adder_1_3_c), .S(S[3]), .C(half_adder_1_4_c));
  half_adder_1 half_adder_1_5 (.A(A[4]), .B(half_adder_1_4_c), .S(S[4]), .C(half_adder_1_5_c));
  half_adder_1 half_adder_1_6 (.A(A[5]), .B(half_adder_1_5_c), .S(S[5]), .C(half_adder_1_6_c));
  half_adder_1 half_adder_1_7 (.A(A[6]), .B(half_adder_1_6_c), .S(S[6]), .C(half_adder_1_7_c));
  half_adder_1 half_adder_1_8 (.A(A[7]), .B(half_adder_1_7_c), .S(S[7]), .C(half_adder_1_8_c));
  half_adder_1 half_adder_1_9 (.A(A[8]), .B(half_adder_1_8_c), .S(S[8]), .C(half_adder_1_9_c));
  half_adder_1 half_adder_1_10 (.A(A[9]), .B(half_adder_1_9_c), .S(S[9]), .C(half_adder_1_10_c));
  half_adder_1 half_adder_1_11 (.A(A[10]), .B(half_adder_1_10_c), .S(S[10]), .C(half_adder_1_11_c));
  half_adder_1 half_adder_1_12 (.A(A[11]), .B(half_adder_1_11_c), .S(S[11]), .C(half_adder_1_12_c));
  half_adder_1 half_adder_1_13 (.A(A[12]), .B(half_adder_1_12_c), .S(S[12]), .C(half_adder_1_13_c));
  half_adder_1 half_adder_1_14 (.A(A[13]), .B(half_adder_1_13_c), .S(S[13]), .C(half_adder_1_14_c));
  half_adder_1 half_adder_1_15 (.A(A[14]), .B(half_adder_1_14_c), .S(S[14]), .C(half_adder_1_15_c));
  half_adder_1 half_adder_1_16 (.A(A[15]), .B(half_adder_1_15_c), .S(S[15]), .C(C));
endmodule

module counter_2 (
  input  RST,
  input  CLK,
  output [1:0] out_3
);

  wire and_1_out, and_2_out, and_3_out, and_4_out, and_5_out, nand_1_out, nand_2_out, not_1_out, not_2_out,
       not_3_out, not_4_out, not_5_out, not_6_out, not_7_out, not_8_out, register_1_3_q, register_1_4_q,
       xor_1_out, xor_2_out;

  not not_1 (not_1_out, CLK);
  not not_2 (not_2_out, not_3_out);
  not not_3 (not_3_out, not_1_out);
  not not_4 (not_4_out, not_6_out);
  not not_5 (not_5_out, not_4_out);
  not not_6 (not_6_out, CLK);
  and and_1 (and_1_out, RST, nand_1_out);
  nand nand_1 (nand_1_out, CLK, not_2_out);
  not not_7 (not_7_out, CLK);
  nand nand_2 (nand_2_out, not_7_out, not_8_out);
  not not_8 (not_8_out, not_5_out);
  and and_2 (and_2_out, register_1_3_q, RST);
  and and_3 (and_3_out, register_1_4_q, RST);
  and and_4 (and_4_out, RST, nand_2_out);
  register_1 register_1_1 (.D(and_2_out), .Q(out_3[0]), .READ(and_1_out));  // open: Q_2
  register_1 register_1_2 (.D(and_3_out), .Q(out_3[1]), .READ(and_1_out));  // open: Q_2
  xor xor_1 (xor_1_out, out_3[0], 1'b1);
  and and_5 (and_5_out, out_3[0], 1'b1);
  xor xor_2 (xor_2_out, out_3[1], and_5_out);
  register_1 register_1_3 (.D(xor_1_out), .Q(register_1_3_q), .READ(and_4_out));  // open: Q_2
  register_1 register_1_4 (.D(xor_2_out), .Q(register_1_4_q), .READ(and_4_out));  // open: Q_2
endmodule

module mod_1_rom (
  input  CLK,
  input  STAT_N,
  input  STAT_Z,
  input  STAT_C,
  input  [15:0] BUS_IN,
  input  RST,
  output EN_BR,
  output [7:0] IR,
  output [15:0] BUS_OUT
);

  wire BR_C_PC, BR_PC, BR_PC_C, BR_PC_D, BR_PC_N, BR_PC_t, BR_PC_Z, BW_ADD, BW_COM, BW_LIT, BW_LIT_t, BW_NOR,
       BW_PC, decoder_inv_2_1_d0, decoder_inv_2_1_d1, decoder_inv_2_1_d2, decoder_inv_2_1_d3,
       decoder_inv_4_1_d0, decoder_inv_4_1_d8, decoder_inv_4_1_d9, decoder_inv_4_1_d13, decoder_inv_4_1_d14,
       decoder_inv_4_1_d15, EN_BR_t, nand_1_out, nand_2_out, nand_3_out, nand_4_out, nand_5_out, nor_1_out,
       nor_6_out, nor_7_out, nor_8_out, nor_9_out, nor_10_out, nor_14_out, nor_15_out, nor_16_out, not_1_out,
       not_2_out, not_5_out, not_6_out, not_7_out, not_8_out, not_9_out, not_11_out, not_12_out, not_13_out,
       not_14_out, register_1_1_q, RST_IR_CNT;
  wire [1:0] counter_2_1_out_3;
  wire [3:0] IR_t_t;
  wire [7:0] IR_t, LIT1, LIT2, rom_1_data;
  wire [15:0] controlled_buffer_1_out, half_adder_16_1_s, PC;

  not not_1 (not_1_out, CLK);
  counter_2 counter_2_1 (.RST(RST_IR_CNT), .CLK(not_1_out), .out_3(counter_2_1_out_3));
  register_8 register_8_1 (.CLK(nor_1_out), .D(rom_1_data), .Q({IR[7:4], IR_t_t}), .Q_2(IR_t));
  nor nor_1 (nor_1_out, not_1_out, decoder_inv_2_1_d0);
  decoder_inv_2 decoder_inv_2_1 (
    .D(counter_2_1_out_3), .D0(decoder_inv_2_1_d0), .D1(decoder_inv_2_1_d1), .D2(decoder_inv_2_1_d2),
    .D3(decoder_inv_2_1_d3));
  nor nor_2 (IR[0], IR_t[0], EN_BR_t);
  nor nor_3 (IR[1], IR_t[1], EN_BR_t);
  nor nor_4 (IR[2], IR_t[2], EN_BR_t);
  nor nor_5 (IR[3], IR_t[3], EN_BR_t);
  decoder_inv_4 decoder_inv_4_1 (
    .D(IR[7:4]), .D0(decoder_inv_4_1_d0), .D6(BW_PC), .D8(decoder_inv_4_1_d8), .D9(decoder_inv_4_1_d9),
    .D10(BW_ADD), .D11(BW_COM), .D12(BW_NOR), .D13(decoder_inv_4_1_d13), .D14(decoder_inv_4_1_d14),
    .D15(decoder_inv_4_1_d15));  // open: D1, D2, D3, D4, D5, D7
  decoder_inv_4 decoder_inv_4_2 (
    .D(IR[3:0]), .D6(BR_PC_D), .D12(BR_C_PC), .D13(BR_PC_C), .D14(BR_PC_Z), .D15(BR_PC_N));  // open: D0, D1, D2, D3, D4, D5, D7, D8, D9, D10, D11
  register_8 register_8_2 (.CLK(nor_6_out), .D(rom_1_data), .Q(LIT1));  // open: Q_2
  nor nor_6 (nor_6_out, not_1_out, decoder_inv_2_1_d1);
  ROM #(.addrWidth(16)) rom_1 (.addr(PC), .data(rom_1_data));  // open: sel
  register_8 register_8_3 (.CLK(nor_7_out), .D(rom_1_data), .Q(LIT2));  // open: Q_2
  nor nor_7 (nor_7_out, not_1_out, decoder_inv_2_1_d2);
  nor nor_8 (nor_8_out, decoder_inv_2_1_d2, BW_LIT_t);
  nor nor_9 (nor_9_out, decoder_inv_2_1_d1, BW_LIT_t);
  nor nor_10 (nor_10_out, decoder_inv_2_1_d3, BW_LIT);
  not not_2 (not_2_out, decoder_inv_4_1_d0);
  nor nor_11 (BW_LIT, not_2_out, nand_1_out);
  nand nand_1 (nand_1_out, decoder_inv_4_1_d8, decoder_inv_4_1_d9, decoder_inv_4_1_d13, decoder_inv_4_1_d14, decoder_inv_4_1_d15);
  nor nor_12 (RST_IR_CNT, nor_8_out, RST);
  nor nor_13 (EN_BR_t, nor_9_out, nor_10_out);
  not not_3 (BW_LIT_t, BW_LIT);
  not not_4 (EN_BR, EN_BR_t);
  not not_5 (not_5_out, not_6_out);
  not not_6 (not_6_out, CLK);
  not not_7 (not_7_out, not_5_out);
  not not_8 (not_8_out, BR_PC_D);
  not not_9 (not_9_out, BR_C_PC);
  nor nor_14 (nor_14_out, BR_PC_N, STAT_N);
  nor nor_15 (nor_15_out, BR_PC_Z, STAT_Z);
  nor nor_16 (nor_16_out, BR_PC_C, STAT_C);
  nand nand_2 (nand_2_out, CLK, not_7_out);
  nor nor_17 (BR_PC, not_8_out, not_9_out, nor_14_out, nor_15_out, nor_16_out);
  not not_10 (BR_PC_t, BR_PC);
  half_adder_16 half_adder_16_1 (.B(1'b1), .A(PC), .S(half_adder_16_1_s));  // open: C
  assign controlled_buffer_1_out = RST ? {16{1'b0}} : 16'bz;  // Controlled_Buffer controlled_buffer_1
  register_1 register_1_1 (.D(EN_BR), .Q(register_1_1_q), .READ(nand_2_out));  // open: Q_2
  not not_11 (not_11_out, RST);
  nand nand_3 (nand_3_out, BR_PC, not_11_out);
  assign controlled_buffer_1_out = not_12_out ? half_adder_16_1_s : 16'bz;  // Controlled_Buffer controlled_buffer_2
  not not_12 (not_12_out, nand_3_out);
  nand nand_4 (nand_4_out, register_1_1_q, BR_PC, not_11_out);
  not not_13 (not_13_out, nand_4_out);
  register_bus_16 register_bus_16_1 (
    .CLK(CLK), .BW(BW_PC), .BR(not_13_out), .BUS_IN(controlled_buffer_1_out), .Q(PC), .BUS_OUT(BUS_OUT));  // open: Q_2
  assign controlled_buffer_1_out = not_14_out ? BUS_IN : 16'bz;  // Controlled_Buffer controlled_buffer_3
  nand nand_5 (nand_5_out, BR_PC_t, not_11_out);
  not not_14 (not_14_out, nand_5_out);
  assign BUS_OUT = BW_LIT_t ? {LIT1, LIT2} : 16'bz;  // Controlled_Buffer controlled_buffer_4

  // Other names for the same wires on the sheet: IR_t_t[7:4] = IR[7:4]

  // Notes on the sheet:
  //   contents of rom_1 (hex, n*v repeats v):
  //   1 0 1 b 0 80 4 0 3f ab 4 0 6 ab 4 0 5b ab 4 0 4f ab 4 0 66 ab 4 0 6d ab 4 0 7d ab 4 0 7 ab 4 0 7f ab
  //   4 0 6f ab 4 0 77 ab 4 0 7c ab 4 0 39 ab 4 0 5e ab 4 0 79 ab 4 0 71 5 1 0 4a c1 2 ff f0 c1 2 0 80 a5
  //   41 5 2 0 14 6 0 45
endmodule

module mod_2_alu (
  input  CLK,
  input  [15:0] BUS_IN,
  input  EN_BR,
  input  [7:0] IR,
  output STAT_N,
  output STAT_Z,
  output STAT_C,
  output [15:0] BUS_OUT
);

  wire ADD_C, BR_A_B, BR_A_D, BR_B_D, BR_B_RP, BR_C_D, BR_C_PC, BR_STAT, BW_A, BW_ADD, BW_B, BW_C, BW_COM,
       BW_NOR, BW_STAT, COM_C, nand_1_out, nand_2_out, nand_4_out, nand_5_out, nor_1_out, nor_3_out,
       nor_4_out, nor_5_out, nor_6_out, nor_7_out, nor_8_out, nor_9_out, not_1_out, not_2_out, not_3_out,
       not_4_out, not_5_out, not_6_out, not_7_out, not_8_out, not_9_out, not_10_out;
  wire [1:0] nor_10_out;
  wire [15:0] A, A_t, adder_16_1_s, B, B_t, controlled_buffer_4_out, half_adder_16_1_s, nor_2_out, STAT;
  wire [15:3] STAT_t;

  decoder_inv_4 decoder_inv_4_1 (
    .D(IR[7:4]), .D1(BW_A), .D2(BW_B), .D3(BW_C), .D7(BW_STAT), .D10(BW_ADD), .D11(BW_COM), .D12(BW_NOR));  // open: D0, D4, D5, D6, D8, D9, D13, D14, D15
  decoder_inv_4 decoder_inv_4_2 (
    .D(IR[3:0]), .D1(BR_A_D), .D2(BR_B_D), .D3(BR_C_D), .D7(BR_STAT), .D10(BR_A_B), .D11(BR_B_RP),
    .D12(BR_C_PC));  // open: D0, D4, D5, D6, D8, D9, D13, D14, D15
  nand nand_1 (nand_1_out, BR_B_D, BR_A_B);
  not not_1 (not_1_out, BR_B_RP);
  not not_2 (not_2_out, CLK);
  not not_3 (not_3_out, nand_2_out);
  nand nand_2 (nand_2_out, BR_A_D, BR_A_B);
  nor nor_1 (nor_1_out, nand_1_out, not_1_out);
  register_bus_16 register_bus_16_1 (
    .CLK(not_2_out), .BW(BW_A), .BR(not_3_out), .BUS_IN(BUS_IN), .Q(A_t), .Q_2(A), .BUS_OUT(BUS_OUT));
  register_bus_16 register_bus_16_2 (
    .CLK(not_2_out), .BW(BW_B), .BR(nor_1_out), .BUS_IN(BUS_IN), .Q(B_t), .Q_2(B), .BUS_OUT(BUS_OUT));
  adder_16 adder_16_1 (.C(1'b0), .B(B_t), .A(A_t), .S(adder_16_1_s), .C_2(ADD_C));
  half_adder_16 half_adder_16_1 (.B(1'b1), .C(COM_C), .A(A), .S(half_adder_16_1_s));
  assign nor_2_out = ~(A_t | B_t);  // NOR_Gate nor_2, 16 bits wide
  assign BUS_OUT = not_4_out ? nor_2_out : 16'bz;  // Controlled_Buffer controlled_buffer_1
  not not_4 (not_4_out, BW_NOR);
  assign BUS_OUT = not_5_out ? adder_16_1_s : 16'bz;  // Controlled_Buffer controlled_buffer_2
  not not_5 (not_5_out, BW_ADD);
  assign BUS_OUT = not_6_out ? half_adder_16_1_s : 16'bz;  // Controlled_Buffer controlled_buffer_3
  not not_6 (not_6_out, BW_COM);
  not not_7 (not_7_out, ADD_C);
  not not_8 (not_8_out, COM_C);
  not not_9 (not_9_out, BUS_IN[0]);
  nor nor_3 (nor_3_out, BUS_IN[15], BUS_IN[14], BUS_IN[13], BUS_IN[12]);
  nor nor_4 (nor_4_out, BUS_IN[11], BUS_IN[10], BUS_IN[9], BUS_IN[8]);
  nor nor_5 (nor_5_out, BUS_IN[7], BUS_IN[6], BUS_IN[5], BUS_IN[4]);
  nor nor_6 (nor_6_out, BUS_IN[3], BUS_IN[2], BUS_IN[1], BUS_IN[0]);
  nor nor_7 (nor_7_out, BW_ADD, not_7_out);
  nor nor_8 (nor_8_out, BW_COM, not_8_out);
  nor nor_9 (nor_9_out, BW_NOR, not_9_out);
  nand nand_3 (nor_10_out[1], nor_3_out, nor_4_out, nor_5_out, nor_6_out);
  nor nor_10 (nor_10_out[0], nor_7_out, nor_8_out, nor_9_out);
  nand nand_4 (nand_4_out, BR_STAT, BW_ADD, BW_COM, BW_NOR);
  nand nand_5 (nand_5_out, nand_4_out, EN_BR);
  assign controlled_buffer_4_out = BR_STAT ? {STAT_t, BUS_IN[15], nor_10_out} : 16'bz;  // Controlled_Buffer controlled_buffer_4
  register_bus_16 register_bus_16_3 (
    .CLK(not_2_out), .BW(BW_STAT), .BR(nand_5_out), .BUS_IN(controlled_buffer_4_out),
    .Q({STAT_t, STAT_N, STAT_Z, STAT_C}), .Q_2(STAT), .BUS_OUT(BUS_OUT));
  assign controlled_buffer_4_out = not_10_out ? BUS_IN : 16'bz;  // Controlled_Buffer controlled_buffer_5
  not not_10 (not_10_out, BR_STAT);

  // Other names for the same wires on the sheet: NOR_C = BUS_IN[0]; STAT_t[2:0] = {STAT_N, STAT_Z, STAT_C}
endmodule

module mod_3_c (
  input  [15:0] BUS_IN,
  input  [7:0] IR,
  input  CLK,
  output [15:0] BUS_OUT
);

  wire decoder_inv_4_1_d3, decoder_inv_4_2_d3, decoder_inv_4_2_d12, nand_1_out, not_1_out, not_2_out;

  decoder_inv_4 decoder_inv_4_1 (
    .D(IR[7:4]), .D3(decoder_inv_4_1_d3));  // open: D0, D1, D2, D4, D5, D6, D7, D8, D9, D10, D11, D12, D13, D14, D15
  decoder_inv_4 decoder_inv_4_2 (
    .D(IR[3:0]), .D3(decoder_inv_4_2_d3), .D12(decoder_inv_4_2_d12));  // open: D0, D1, D2, D4, D5, D6, D7, D8, D9, D10, D11, D13, D14, D15
  not not_1 (not_1_out, nand_1_out);
  nand nand_1 (nand_1_out, decoder_inv_4_2_d3, decoder_inv_4_2_d12);
  not not_2 (not_2_out, CLK);
  register_bus_16 register_bus_16_1 (
    .CLK(not_2_out), .BW(decoder_inv_4_1_d3), .BR(not_1_out), .BUS_IN(BUS_IN), .BUS_OUT(BUS_OUT));  // open: Q, Q_2
endmodule

module mod_4_ram (
  input  CLK,
  input  [15:0] BUS_IN,
  input  [7:0] IR,
  output [15:0] BUS_OUT
);

  wire BR_B_RP, BR_RAM, BR_RAM_t, BR_RP_D, BW_RAM, BW_RAM_t, BW_RP, nand_1_out, nand_2_out, nand_3_out,
       nand_4_out, nor_1_out, nor_2_out, nor_3_out, nor_4_out, nor_5_out, not_1_out, not_2_out, not_5_out,
       not_6_out, not_7_out, xor_1_out;
  wire [3:0] joystick_1_x, joystick_1_y, register_16_1_q_2;
  wire [15:0] register_16_1_q, register_bus_16_1_q;
  wire [15:8] button_1_out;

  not not_1 (not_1_out, CLK);
  not not_2 (not_2_out, nand_1_out);
  nand nand_1 (nand_1_out, BR_RP_D, BR_B_RP);
  decoder_inv_4 decoder_inv_4_1 (
    .D(IR[7:4]), .D4(BW_RAM), .D5(BW_RP));  // open: D0, D1, D2, D3, D6, D7, D8, D9, D10, D11, D12, D13, D14, D15
  decoder_inv_4 decoder_inv_4_2 (
    .D(IR[3:0]), .D4(BR_RAM), .D5(BR_RP_D), .D11(BR_B_RP));  // open: D0, D1, D2, D3, D6, D7, D8, D9, D10, D12, D13, D14, D15
  register_bus_16 register_bus_16_1 (
    .CLK(not_1_out), .BW(BW_RP), .BR(not_2_out), .BUS_IN(BUS_IN), .Q(register_bus_16_1_q), .BUS_OUT(BUS_OUT));  // open: Q_2
  not not_3 (BW_RAM_t, BW_RAM);
  not not_4 (BR_RAM_t, BR_RAM);
  nor nor_1 (nor_1_out, BR_RAM, not_1_out);
  nor nor_2 (nor_2_out, BW_RAM, register_bus_16_1_q[8]);
  nor nor_3 (nor_3_out, register_bus_16_1_q[15], register_bus_16_1_q[14], register_bus_16_1_q[13], register_bus_16_1_q[12], register_bus_16_1_q[11]);
  nor nor_4 (nor_4_out, register_bus_16_1_q[10], register_bus_16_1_q[7], register_bus_16_1_q[6], register_bus_16_1_q[5], register_bus_16_1_q[4]);
  nor nor_5 (nor_5_out, register_bus_16_1_q[3], register_bus_16_1_q[2], register_bus_16_1_q[1], register_bus_16_1_q[0]);
  RAM #(.addrWidth(16), .bus("separate")) ram_1 (
    .addr(register_bus_16_1_q), .din(BUS_IN[15:8]), .data(BUS_OUT[15:8]), .clk(nor_1_out), .ld(nor_2_out));  // open: str, sel, clr
  RAM #(.addrWidth(16), .bus("separate")) ram_2 (
    .addr(register_bus_16_1_q), .din(BUS_IN[7:0]), .data(BUS_OUT[7:0]), .clk(nor_1_out), .ld(nor_2_out));  // open: str, sel, clr
  xor xor_1 (xor_1_out, register_bus_16_1_q[9], register_bus_16_1_q[8]);
  nand nand_2 (nand_2_out, xor_1_out, nor_3_out, nor_4_out, nor_5_out);
  not not_5 (not_5_out, nand_2_out);
  assign BUS_OUT = not_6_out ? {button_1_out, joystick_1_x, joystick_1_y} : 16'bz;  // Controlled_Buffer controlled_buffer_1
  not not_6 (not_6_out, nand_3_out);
  nand nand_3 (nand_3_out, register_bus_16_1_q[8], not_5_out, BW_RAM_t);
  register_16 register_16_1 (
    .CLK(not_7_out), .D(BUS_IN), .Q({register_16_1_q[15:12], register_16_1_q_2, register_16_1_q[7:0]}));  // open: Q_2
  not not_7 (not_7_out, nand_4_out);
  nand nand_4 (nand_4_out, register_bus_16_1_q[9], not_5_out, CLK, BR_RAM_t);
  Button button_1 (.out(button_1_out[8]));
  Button button_2 (.out(button_1_out[10]));
  Button button_3 (.out(button_1_out[12]));
  Button button_4 (.out(button_1_out[14]));
  Joystick joystick_1 (.x(joystick_1_x), .y(joystick_1_y));
  Hex_Digit_Display hex_digit_display_1 (.value(register_16_1_q[15:12]));  // open: dp
  Hex_Digit_Display hex_digit_display_2 (.value(register_16_1_q_2));  // open: dp
  Button button_5 (.out(button_1_out[9]));
  Button button_6 (.out(button_1_out[11]));
  Button button_7 (.out(button_1_out[13]));
  Button button_8 (.out(button_1_out[15]));
  Hex_Digit_Display hex_digit_display_3 (.value(register_16_1_q[7:4]));  // open: dp
  LED led_1 (.in(register_16_1_q[15]));
  LED led_2 (.in(register_16_1_q[14]));
  LED led_3 (.in(register_16_1_q[13]));
  LED led_4 (.in(register_16_1_q[12]));
  LED led_5 (.in(register_16_1_q_2[3]));
  LED led_6 (.in(register_16_1_q_2[2]));
  LED led_7 (.in(register_16_1_q_2[1]));
  LED led_8 (.in(register_16_1_q_2[0]));
  _7_Segment_Display u_7_segment_display_1 (
    .g(register_16_1_q[6]), .f(register_16_1_q[5]), .a(register_16_1_q[0]), .b(register_16_1_q[1]),
    .e(register_16_1_q[4]), .d(register_16_1_q[3]), .c(register_16_1_q[2]), .dp(register_16_1_q[7]));
  Hex_Digit_Display hex_digit_display_4 (.value(register_16_1_q[3:0]));  // open: dp

  // Notes on the sheet:
  //   0x0100 (GPIA)
  //   0x0200 (GPOA)
endmodule
